# Fritzing sketch everyESP485 (saved by Fritzing 1.0.3b)
circuit board: 5.63181cm x 5.10695cm

parts:
  Component1 = RS485_XY-017 [part_number=XY-017]
  M1 = RioRand LM2596
  J1 = male pin header, 4 pins [form="♂ (male)"]
  J2 = female pin header, 8 pins [form="♀ (female)"]
  J3 = female pin header, 8 pins [form="♀ (female)"]
  WeMos_D1_Mini1 = WeMos D1 Mini  # not connected

nets:
  N1: Component1.GND#0, M1.Pin_4, J2.pin7
  N2: Component1.A, J1.pin4
  N3: Component1.B, J1.pin3
  N4: Component1.VCC, M1.Pin_3, J3.pin8
  N5: Component1.TXD, J2.pin1
  N6: Component1.GND#5, M1.Pin_2, J1.pin2
  N7: Component1.RXD, J2.pin2
  N8: M1.Pin_1, J1.pin1

custom parts:
  RS485_XY-017: Commercially available RS485 to RS232 TTL Module
