# Fritzing sketch everyESP485_wtAMS1117 (saved by Fritzing 1.0.3b)
circuit board: 6.74875cm x 5.00722cm

parts:
  WeMos_D1_Mini1 = WeMos D1 Mini
  U1 = V_REG_LD1117VXX [package=78xxl]
  H1 = polarizedheader 4pin 0.156in [package=THT]
  Component2 = RS485_XY-017_mir [part_number=XY-017]

nets:
  3V3: WeMos_D1_Mini1.3V3, Component2.VCC
  N1: WeMos_D1_Mini1.5V, U1.OUT
  N2: WeMos_D1_Mini1.G, U1.GND, Component2.GND#0
  N3: WeMos_D1_Mini1.RX, Component2.RXD
  N4: WeMos_D1_Mini1.TX, Component2.TXD
  N5: U1.IN, H1.pin4
  N6: H1.pin1, Component2.A
  N7: H1.pin2, Component2.B
  N8: H1.pin3, Component2.GND#5

notes:
  [1] [2] [3] [4]
  RX RX GND 12V
  [1] RX
  [2] TX
  [3] GND
  [4] 12V

custom parts:
  RS485_XY-017_mir: Commercially available RS485 to RS232 TTL Module
